# Fritzing sketch Diagrama (saved by Fritzing 0.9.3b)
breadboards: 1

parts:
  Componente1 = Arduino Uno (Rev3)
  D1 = LED_BARGRAPH_10 [package=led_bargaph_8]
  R1 = Resistor [tolerance=±5% resistance=220 package=THT]

nets:
  N1: Componente1.D8, D1.H_C
  N2: Componente1.D9_PWM, D1.G_C
  N3: Componente1.D10_PWM/SS, D1.F_C
  N4: Componente1.D11_PWM/MOSI, D1.E_C
  N5: Componente1.D12/MISO, D1.D_C
  N6: Componente1.D13/SCK, D1.C_C
  N7: Componente1.GND, R1.Pin_0
  N8: D1.C_A, D1.D_A, D1.E_A, D1.F_A, D1.G_A, D1.H_A, R1.Pin_1

custom parts:
  LED_BARGRAPH_10: 8-Segment LED Bar Graph
